# Fritzing sketch nodemcu_odoo (saved by Fritzing 0.8.5b)
breadboards: 1

parts:
  U1 = NodeMCU V3.0
  Parte1 = RFID-RC522-v2
  S1 = Pushbutton [package="[THT]"]
  LED1 = LED - 5mm [color="Green (555nm)" package="5 mm [THT]"]
  R1 = Resistor [tolerance=±5% resistance=220 package=THT]
  LED2 = LED - 5mm [color="Red (633nm)" package="5 mm [THT]"]
  R2 = Resistor [tolerance=±5% resistance=220 package=THT]
  J1 = Piezo Speaker

nets:
  N1: U1.D0, S1.Pin_1, S1.Pin_2
  N2: U1.D1, LED1.anode
  N3: U1.D2, LED2.anode
  N4: U1.D3, Parte1.RST
  N5: U1.D4, Parte1.SDA
  N6: U1.D5, Parte1.SCK
  N7: U1.D6, Parte1.MISO
  N8: U1.D7, Parte1.MOSI
  N9: U1.D8, J1.pin2
  GND: U1.GND, Parte1.GND, S1.Pin_3, S1.Pin_4, R1.Pin_0, R2.Pin_0, J1.pin1
  3V3: U1.3V3, Parte1.3.3V
  N10: LED2.cathode, R2.Pin_1

custom parts:
  NodeMCU V3.0: ESP8266 based NodeMCU
  RFID-RC522-v2: A simple China made RFID-RC522 Reader; do check the pin labels, as this is a MFRC522 based clone.
